// Logisim project ULA IC.circ as structural Verilog: 7 circuits, main circuit Somador Completo
// +
module Somador_Completo (
  input  A1,
  input  B1,
  input  A2,
  input  B2,
  output out_5,
  output out_6,
  output out_7
);

  wire and_1_out, and_2_out, and_3_out, and_4_out, and_5_out, and_6_out, or_2_out, xor_1_out, xor_3_out;

  ExactlyOne xor_1 (.out(xor_1_out), .in0(A2), .in1(B2), .in2(or_2_out));
  and and_1 (and_1_out, or_2_out, A2);
  and and_2 (and_2_out, or_2_out, B2);
  and and_3 (and_3_out, B2, A2);
  xor xor_2 (out_6, xor_1_out, or_2_out);
  or or_1 (out_5, and_1_out, and_2_out, and_3_out);
  ExactlyOne xor_3 (.out(xor_3_out), .in0(A1), .in1(B1), .in2(1'b0));
  and and_4 (and_4_out, 1'b0, A1);
  and and_5 (and_5_out, 1'b0, B1);
  and and_6 (and_6_out, B1, A1);
  xor xor_4 (out_7, xor_3_out, 1'b0);
  or or_2 (or_2_out, and_4_out, and_5_out, and_6_out);
endmodule

module ALU_2Bits (
  input  [1:0] in_1,
  input  [1:0] in_2,
  input  [1:0] in_3,
  output [2:0] out_4,
  output [2:0] out_5
);

  Somador_Completo somador_completo (
    .A2(in_1[1]), .B2(in_2[1]), .A1(in_1[0]), .B1(in_2[0]), .out_5(out_4[2]), .out_6(out_4[1]),
    .out_7(out_4[0]));
  Subtrador_Completo subtrador_completo (
    .A2(in_1[1]), .B2(in_2[1]), .A1(in_1[0]), .B1(in_2[0]), .out_6(out_5[2]), .out_7(out_5[1]),
    .out_8(out_5[0]));  // open: out_5
  MUX_4x1 mux_4x1_1 (.A1(in_3[0]), .A2(in_3[1]));  // open: in_1, in_2, in_3, in_4, out_7
  Divisor divisor_1 ();  // open: A1, A0, B1, B0, Q1, Q0, R1, R0, E
  Multiplicador multiplicador_1 ();  // open: A1, A2, B1, B2, R1, R2, R3, R4
endmodule

// -
module Subtrador_Completo (
  input  A1,
  input  B1,
  input  A2,
  input  B2,
  output out_5,
  output out_6,
  output out_7,
  output out_8
);

  wire and_1_out, and_2_out, and_3_out, and_4_out, and_5_out, and_6_out, not_1_out, not_2_out, not_3_out,
       not_4_out, xor_1_out, xor_3_out;

  not not_1 (not_1_out, A2);
  not not_2 (not_2_out, A2);
  xor xor_1 (xor_1_out, A2, B2);
  and and_1 (and_1_out, not_1_out, B2);
  and and_2 (and_2_out, not_2_out, out_5);
  and and_3 (and_3_out, B2, out_5);
  xor xor_2 (out_7, xor_1_out, out_5);
  or or_1 (out_6, and_1_out, and_2_out, and_3_out);
  not not_3 (not_3_out, A1);
  not not_4 (not_4_out, A1);
  xor xor_3 (xor_3_out, A1, B1);
  and and_4 (and_4_out, not_3_out, B1);
  and and_5 (and_5_out, not_4_out, 1'b0);
  and and_6 (and_6_out, B1, 1'b0);
  xor xor_4 (out_8, xor_3_out, 1'b0);
  or or_2 (out_5, and_4_out, and_5_out, and_6_out);
endmodule

module MUX_4x1 (
  input  in_1,
  input  in_2,
  input  in_3,
  input  in_4,
  input  A1,
  input  A2,
  output out_7
);

  wire and_1_out, and_2_out, and_3_out, and_4_out, and_5_out, and_6_out, and_7_out, and_8_out, not_1_out,
       not_2_out, not_3_out, not_4_out;

  not not_1 (not_1_out, A1);
  not not_2 (not_2_out, A2);
  not not_3 (not_3_out, A1);
  not not_4 (not_4_out, A2);
  and and_1 (and_1_out, not_1_out, not_2_out);
  and and_2 (and_2_out, not_3_out, A2);
  and and_3 (and_3_out, A1, not_4_out);
  and and_4 (and_4_out, A1, A2);
  and and_5 (and_5_out, in_1, and_1_out);
  and and_6 (and_6_out, in_2, and_2_out);
  and and_7 (and_7_out, in_3, and_3_out);
  and and_8 (and_8_out, in_4, and_4_out);
  or or_1 (out_7, and_5_out, and_6_out, and_7_out, and_8_out);
endmodule

// X
module Multiplicador (
  input  A1,
  input  A2,
  input  B1,
  input  B2,
  output R1,
  output R2,
  output R3,
  output R4
);

  wire and_2_out, and_3_out, and_4_out, and_5_out, and_6_out, and_7_out, not_1_out, not_2_out, not_3_out,
       not_4_out, not_5_out, not_6_out;

  and and_1 (R1, A1, A2, B1, B2);
  not not_1 (not_1_out, A2);
  and and_2 (and_2_out, A1, not_1_out, B1);
  and and_3 (and_3_out, A1, B1, not_2_out);
  not not_2 (not_2_out, B2);
  not not_3 (not_3_out, A1);
  and and_4 (and_4_out, not_3_out, A2, B1);
  and and_5 (and_5_out, A2, B1, not_4_out);
  not not_4 (not_4_out, B2);
  and and_6 (and_6_out, A1, not_5_out, B2);
  not not_5 (not_5_out, A2);
  not not_6 (not_6_out, B1);
  and and_7 (and_7_out, A1, not_6_out, B2);
  and and_8 (R4, A2, B2);
  or or_1 (R2, and_2_out, and_3_out);
  or or_2 (R3, and_4_out, and_5_out, and_6_out, and_7_out);
endmodule

// :
module Divisor (
  input  A1,
  input  A0,
  input  B1,
  input  B0,
  output Q1,
  output Q0,
  output R1,
  output R0,
  output E
);

  wire and_1_out, and_2_out, and_3_out, and_4_out, and_5_out, and_6_out, and_7_out, not_1_out, not_2_out,
       not_3_out, not_4_out, not_5_out, not_6_out, not_7_out, not_8_out;

  not not_1 (not_1_out, B1);
  and and_1 (and_1_out, A1, not_1_out, B0);
  and and_2 (and_2_out, A1, A0, B0);
  and and_3 (and_3_out, A0, not_2_out, B0);
  not not_2 (not_2_out, B1);
  and and_4 (and_4_out, A1, B1, not_3_out);
  not not_3 (not_3_out, B0);
  and and_5 (and_5_out, A1, A0, B1);
  not not_4 (not_4_out, A0);
  not not_5 (not_5_out, A1);
  and and_6 (and_6_out, not_5_out, A0, B1);
  and and_7 (and_7_out, A0, B1, not_6_out);
  not not_6 (not_6_out, B0);
  not not_7 (not_7_out, B1);
  and and_8 (E, not_7_out, not_8_out);
  not not_8 (not_8_out, B0);
  or or_1 (Q1, and_1_out, and_2_out);
  or or_2 (Q0, and_3_out, and_4_out, and_5_out);
  and and_9 (R1, A1, not_4_out, B1, B0);
  or or_3 (R0, and_6_out, and_7_out);
endmodule

module teste (
  input  in_1,
  input  in_2,
  input  in_3,
  input  in_4,
  input  in_5,
  output [1:0] out_6
);

  Multiplexer #(.select(2), .width(2)) multiplexer_1 (
    .in1({in_2, in_1}), .in3({in_4, in_3}), .out(out_6), .en(in_5));  // open: in0, in2, sel
endmodule
